// Logisim project NEW_PJ.circ as structural Verilog
module BUS (
);

  wire alu16bit_1_e_out, and_1_out, and_2_out, and_3_out, and_4_out, clock_1_out, control_unit_1_clr_ac,
       control_unit_1_clr_ar, control_unit_1_clr_dr, control_unit_1_clr_pc, control_unit_1_cme,
       control_unit_1_inr_ac, control_unit_1_inr_ar, control_unit_1_inr_dr, control_unit_1_inr_pc,
       control_unit_1_lda_ac, control_unit_1_lda_ar, control_unit_1_lda_dr, control_unit_1_lda_ir,
       control_unit_1_lda_pc, control_unit_1_ram_read, control_unit_1_ram_write, E_qn, or_1_out, or_2_out;
  wire [0:0] E_q;
  wire [2:0] control_unit_1_mux_select;
  wire [7:0] control_unit_1_alu;
  wire [11:0] counter_1_q, counter_2_q, n16to12_1_out_2, n16to12_2_out_2;
  wire [15:0] alu16bit_1_ac_i, counter_3_q, counter_4_q, counter_5_q, multiplexer_1_out, n12to16_1_out_2,
       n12to16_2_out_2, ram_1_data;

  Control_Unit control_unit_1 (
    .DR(counter_3_q), .IR(counter_5_q), .AC(counter_4_q), .E(E_q[0]), .LDA_AR(control_unit_1_lda_ar),
    .CLR_AR(control_unit_1_clr_ar), .INR_AR(control_unit_1_inr_ar), .LDA_IR(control_unit_1_lda_ir),
    .LDA_PC(control_unit_1_lda_pc), .CLR_PC(control_unit_1_clr_pc), .INR_PC(control_unit_1_inr_pc),
    .LDA_DR(control_unit_1_lda_dr), .CLR_DR(control_unit_1_clr_dr), .INR_DR(control_unit_1_inr_dr),
    .LDA_AC(control_unit_1_lda_ac), .CLR_AC(control_unit_1_clr_ac), .INR_AC(control_unit_1_inr_ac),
    .cp(clock_1_out), .ALU(control_unit_1_alu), .RAM_READ(control_unit_1_ram_read),
    .RAM_WRITE(control_unit_1_ram_write), .MUX_SELECT(control_unit_1_mux_select), .CME(control_unit_1_cme));
  and and_1 (and_1_out, control_unit_1_cme, E_qn);
  and and_2 (and_2_out, control_unit_1_alu[1], alu16bit_1_e_out);
  or or_1 (or_1_out, and_2_out, and_3_out, and_1_out, and_4_out);
  D_Flip_Flop E (.clk(clock_1_out), .D(or_1_out), .Q(E_q[0]), .Qn(E_qn), .en(or_2_out));  // open: preset, reset
  or or_2 (or_2_out, control_unit_1_alu[5], control_unit_1_alu[4], control_unit_1_cme, control_unit_1_alu[1]);
  and and_3 (and_3_out, counter_4_q[15], control_unit_1_alu[5]);
  and and_4 (and_4_out, counter_4_q[0], control_unit_1_alu[4]);
  _16To12 u_16to12_1 (.inp(multiplexer_1_out), .out_2(n16to12_1_out_2));
  _16To12 u_16to12_2 (.inp(multiplexer_1_out), .out_2(n16to12_2_out_2));
  ALU16bit alu16bit_1 (
    .CU_inputs(control_unit_1_alu[5:0]), .E_in(E_q[0]), .DR(counter_3_q), .AC_i(alu16bit_1_ac_i),
    .AC_i_1({E_q[0], counter_4_q[15:1]}), .AC_i_1_2({counter_4_q[14:0], E_q[0]}), .AC(counter_4_q),
    .E_out(alu16bit_1_e_out));
  Clock clock_1 (.out(clock_1_out));
  RAM #(.addrWidth(12), .dataWidth(16), .bus("separate")) ram_1 (
    .addr(counter_1_q), .din(multiplexer_1_out), .data(ram_1_data), .str(control_unit_1_ram_write),
    .clk(clock_1_out), .ld(control_unit_1_ram_read));  // open: sel, clr
  Counter #(.width(12), .max('hfff)) counter_1 (
    .load(control_unit_1_lda_ar), .D(n16to12_1_out_2), .count(control_unit_1_inr_ar), .Q(counter_1_q),
    .clk(clock_1_out), .clr(control_unit_1_clr_ar));  // open: carry
  Counter #(.width(12), .max('hfff)) counter_2 (
    .load(control_unit_1_lda_pc), .D(n16to12_2_out_2), .count(control_unit_1_inr_pc), .Q(counter_2_q),
    .clk(clock_1_out), .clr(control_unit_1_clr_pc));  // open: carry
  Counter #(.width(16), .max('hffff)) counter_3 (
    .load(control_unit_1_lda_dr), .D(multiplexer_1_out), .count(control_unit_1_inr_dr), .Q(counter_3_q),
    .clk(clock_1_out), .clr(control_unit_1_clr_dr));  // open: carry
  Counter #(.width(16), .max('hffff)) counter_4 (
    .load(control_unit_1_lda_ac), .D(alu16bit_1_ac_i), .count(control_unit_1_inr_ac), .Q(counter_4_q),
    .clk(clock_1_out), .clr(control_unit_1_clr_ac));  // open: carry
  Counter #(.width(16), .max('hffff)) counter_5 (
    .load(control_unit_1_lda_ir), .D(multiplexer_1_out), .count(1'b0), .Q(counter_5_q), .clk(clock_1_out));  // open: carry, clr
  _12To16 u_12to16_1 (.inp(counter_1_q), .out_2(n12to16_1_out_2));
  _12To16 u_12to16_2 (.inp(counter_2_q), .out_2(n12to16_2_out_2));
  Multiplexer #(.select(3), .width(16), .enable("false")) multiplexer_1 (
    .in1(n12to16_1_out_2), .in2(n12to16_2_out_2), .in3(counter_3_q), .in4(counter_4_q), .in5(counter_5_q),
    .in7(ram_1_data), .out(multiplexer_1_out), .sel(control_unit_1_mux_select));  // open: in0, in6
endmodule

module Control_Unit (
  input  [15:0] DR,
  input  [15:0] IR,
  input  [15:0] AC,
  input  E,
  input  cp,
  output LDA_AR,
  output CLR_AR,
  output INR_AR,
  output LDA_IR,
  output LDA_PC,
  output CLR_PC,
  output INR_PC,
  output LDA_DR,
  output CLR_DR,
  output INR_DR,
  output LDA_AC,
  output CLR_AC,
  output INR_AC,
  output [7:0] ALU,
  output RAM_READ,
  output RAM_WRITE,
  output [2:0] MUX_SELECT,
  output CME
);

  wire and_1_out, and_2_out, d_ff_1_q, decoder_1_out0, decoder_1_out1, decoder_1_out2, decoder_1_out3,
       decoder_1_out4, decoder_1_out5, decoder_1_out6, decoder_1_out7, decoder_2_out0, decoder_2_out1,
       decoder_2_out2, decoder_2_out3, decoder_2_out4, decoder_2_out5, decoder_2_out6, not_1_out, not_2_out,
       r_out, S_q, sc_control_1_sc_clear;
  wire [2:0] counter_1_q;

  D_Flip_Flop d_ff_1 (.clk(cp), .D(IR[15]), .Q(d_ff_1_q));  // open: Qn, preset, en, reset
  Counter #(.width(3), .max('h7)) counter_1 (
    .load(sc_control_1_sc_clear), .D(3'b000), .count(and_1_out), .Q(counter_1_q), .clk(cp));  // open: carry, clr
  D_Flip_Flop S (.clk(cp), .D(not_2_out), .Q(S_q));  // open: Qn, preset, en, reset
  and and_1 (and_1_out, S_q, ~sc_control_1_sc_clear);  // AND_Gate
  Decoder #(.select(3), .enable("false")) decoder_1 (
    .out0(decoder_1_out0), .out1(decoder_1_out1), .out2(decoder_1_out2), .out3(decoder_1_out3),
    .out4(decoder_1_out4), .out5(decoder_1_out5), .out6(decoder_1_out6), .out7(decoder_1_out7),
    .sel(IR[14:12]));
  Decoder #(.select(3), .enable("false")) decoder_2 (
    .out0(decoder_2_out0), .out1(decoder_2_out1), .out2(decoder_2_out2), .out3(decoder_2_out3),
    .out4(decoder_2_out4), .out5(decoder_2_out5), .out6(decoder_2_out6), .sel(counter_1_q));  // open: out7
  not not_1 (not_1_out, d_ff_1_q);
  not not_2 (not_2_out, and_2_out);
  and and_2 (and_2_out, IR[0], r_out);
  and r (r_out, decoder_1_out7, not_1_out, decoder_2_out3);
  and and_3 (CME, r_out, IR[8]);
  AR_Contorl AR (
    .D5(decoder_1_out5), .D7(decoder_1_out7), .I(d_ff_1_q), .T0(decoder_2_out0), .T2(decoder_2_out2),
    .T3(decoder_2_out3), .T4(decoder_2_out4), .LDA(LDA_AR), .CLR(CLR_AR), .INR(INR_AR));
  IR_Control ir_control_1 (.T1(decoder_2_out1), .LDA(LDA_IR));  // open: CLR, INR
  PC_Control pc_control_1 (
    .T1(decoder_2_out1), .T4(decoder_2_out4), .T5(decoder_2_out5), .T6(decoder_2_out6), .D4(decoder_1_out4),
    .D5(decoder_1_out5), .D6(decoder_1_out6), .r(r_out), .B4(IR[4]), .B3(IR[3]), .B2(IR[2]), .B1(IR[1]),
    .E(E), .DR(DR), .AC(AC), .LDA(LDA_PC), .CLR(CLR_PC), .INR(INR_PC));
  DR_Control dr_control_1 (
    .T4(decoder_2_out4), .T5(decoder_2_out5), .D0(decoder_1_out0), .D1(decoder_1_out1), .D2(decoder_1_out2),
    .D6(decoder_1_out6), .LDA(LDA_DR), .CLR(CLR_DR), .INR(INR_DR));
  AC_Control u_AC (
    .T5(decoder_2_out5), .D0(decoder_1_out0), .D1(decoder_1_out1), .D2(decoder_1_out2), .r(r_out),
    .B11(IR[11]), .B9(IR[9]), .B7(IR[7]), .B6(IR[6]), .B5(IR[5]), .LDA(LDA_AC), .CLR(CLR_AC), .INR(INR_AC),
    .ALU(ALU));
  Memory_Control RAM (
    .T1(decoder_2_out1), .T3(decoder_2_out3), .T4(decoder_2_out4), .T6(decoder_2_out6), .D0(decoder_1_out0),
    .D1(decoder_1_out1), .D2(decoder_1_out2), .D3(decoder_1_out3), .D5(decoder_1_out5), .D6(decoder_1_out6),
    .D7(decoder_1_out7), .I(d_ff_1_q), .Read(RAM_READ), .Write(RAM_WRITE));
  MUX_Control mux_control_1 (
    .D0(decoder_1_out0), .D1(decoder_1_out1), .D2(decoder_1_out2), .D3(decoder_1_out3), .D4(decoder_1_out4),
    .D5(decoder_1_out5), .D6(decoder_1_out6), .D7(decoder_1_out7), .T1(decoder_2_out1), .T2(decoder_2_out2),
    .T3(decoder_2_out3), .T4(decoder_2_out4), .T5(decoder_2_out5), .T6(decoder_2_out6), .I(d_ff_1_q),
    .T0(decoder_2_out0), .SELECT_MUX(MUX_SELECT));
  SC_Control sc_control_1 (
    .D0(decoder_1_out0), .D1(decoder_1_out1), .D2(decoder_1_out2), .D3(decoder_1_out3), .D4(decoder_1_out4),
    .D5(decoder_1_out5), .D6(decoder_1_out6), .T4(decoder_2_out4), .T5(decoder_2_out5), .T6(decoder_2_out6),
    .r(r_out), .SC_Clear(sc_control_1_sc_clear));
endmodule

module _16To12 (
  input  [15:0] inp,
  output [11:0] out_2
);


  assign out_2 = inp[11:0];
endmodule

module _12To16 (
  input  [11:0] inp,
  output [15:0] out_2
);


  assign out_2[11:0] = inp;
endmodule

module AR_Contorl (
  input  D5,
  input  D7,
  input  I,
  input  T0,
  input  T2,
  input  T3,
  input  T4,
  output LDA,
  output CLR,
  output INR
);

  wire and_1_out, not_1_out;

  not not_1 (not_1_out, D7);
  and and_1 (and_1_out, not_1_out, I, T3);
  or or_1 (LDA, T0, T2, and_1_out);
  and and_2 (INR, D5, T4);

  assign CLR = 1'b0;
endmodule

// PC
module PC_Control (
  input  T1,
  input  T4,
  input  T5,
  input  T6,
  input  D4,
  input  D5,
  input  D6,
  input  r,
  input  B4,
  input  B3,
  input  B2,
  input  B1,
  input  E,
  input  [15:0] DR,
  input  [15:0] AC,
  output LDA,
  output CLR,
  output INR
);

  wire _0_2_zero_register, _0_zero_register, _15__15th, and_1_out, and_2_out, and_3_out, and_4_out,
       and_5_out, and_6_out, and_7_out, not_1_out, not_2_out;

  _0_Register _0 (.Register(DR), .Zero_Register(_0_zero_register));
  Register_15 _15 (.Register(AC), ._15th(_15__15th));
  _0_Register _0_2 (.Register(AC), .Zero_Register(_0_2_zero_register));
  not not_1 (not_1_out, _15__15th);
  not not_2 (not_2_out, E);
  and and_1 (and_1_out, D4, T4);
  and and_2 (and_2_out, D5, T5);
  and and_3 (and_3_out, D6, T6, _0_zero_register);
  and and_4 (and_4_out, r, B4, not_1_out);
  and and_5 (and_5_out, r, B3, _15__15th);
  and and_6 (and_6_out, r, B2, _0_2_zero_register);
  and and_7 (and_7_out, r, B1, not_2_out);
  or or_1 (LDA, and_1_out, and_2_out);
  or or_2 (INR, T1, and_3_out, and_4_out, and_5_out, and_6_out, and_7_out);

  assign CLR = 1'b0;
endmodule

// IR
module IR_Control (
  input  T1,
  output LDA,
  output CLR,
  output INR
);


  assign CLR = 1'b0;
  assign INR = 1'b0;
  assign LDA = T1;
endmodule

// DR
module DR_Control (
  input  T4,
  input  T5,
  input  D0,
  input  D1,
  input  D2,
  input  D6,
  output LDA,
  output CLR,
  output INR
);

  wire and_1_out, and_2_out, and_3_out, and_4_out;

  and and_1 (and_1_out, D0, T4);
  and and_2 (and_2_out, D1, T4);
  and and_3 (and_3_out, D2, T4);
  and and_4 (and_4_out, D6, T4);
  and and_5 (INR, D6, T5);
  or or_1 (LDA, and_1_out, and_2_out, and_3_out, and_4_out);

  assign CLR = 1'b0;
endmodule

module MUX_Control (
  input  D0,
  input  D1,
  input  D2,
  input  D3,
  input  D4,
  input  D5,
  input  D6,
  input  D7,
  input  T1,
  input  T2,
  input  T3,
  input  T4,
  input  T5,
  input  T6,
  input  I,
  input  T0,
  output [2:0] SELECT_MUX
);

  wire and_1_out, and_2_out, and_3_out, and_4_out, and_5_out, and_6_out, and_7_out, and_8_out, and_9_out,
       and_10_out, not_1_out, or_1_out, or_2_out, x1_out, x3_out, x4_out, x7_out;

  not not_1 (not_1_out, D7);
  and and_1 (and_1_out, D4, T4);
  and and_2 (and_2_out, D5, T5);
  and and_3 (and_3_out, not_1_out, I, T3);
  and and_4 (and_4_out, D0, T4);
  and and_5 (and_5_out, D1, T4);
  and and_6 (and_6_out, D2, T4);
  and and_7 (and_7_out, D3, T4);
  and and_8 (and_8_out, D2, T5);
  and and_9 (and_9_out, D6, T6);
  and x4 (x4_out, D3, T4);
  and and_10 (and_10_out, D5, T4);
  or or_1 (or_1_out, and_7_out, x4_out);
  or x1 (x1_out, and_1_out, and_2_out);
  or x7 (x7_out, and_3_out, and_4_out, and_5_out, and_6_out, T1);
  or x3 (x3_out, and_8_out, and_9_out);
  or or_2 (or_2_out, and_10_out, T0);
  or s2 (SELECT_MUX[2], x1_out, x3_out, or_1_out, T2, x7_out);
  or s1 (SELECT_MUX[1], or_2_out, x3_out, x7_out);
  or s0 (SELECT_MUX[0], T2, x7_out);

  // Notes on the sheet:
  //   x2
  //   x5
endmodule

module Memory_Control (
  input  T1,
  input  T3,
  input  T4,
  input  T6,
  input  D0,
  input  D1,
  input  D2,
  input  D3,
  input  D5,
  input  D6,
  input  D7,
  input  I,
  output Read,
  output Write
);

  wire and_1_out, and_2_out, and_3_out, and_4_out, and_5_out, and_6_out, and_7_out, and_8_out, not_1_out;

  not not_1 (not_1_out, D7);
  and and_1 (and_1_out, not_1_out, I, T3);
  and and_2 (and_2_out, D0, T4);
  and and_3 (and_3_out, D1, T4);
  and and_4 (and_4_out, D2, T4);
  and and_5 (and_5_out, D6, T4);
  and and_6 (and_6_out, D3, T4);
  and and_7 (and_7_out, D5, T4);
  and and_8 (and_8_out, not_1_out, T6);
  or or_1 (Read, T1, and_1_out, and_2_out, and_3_out, and_4_out, and_5_out);
  or or_2 (Write, and_6_out, and_7_out, and_8_out);
endmodule

module SC_Control (
  input  D0,
  input  D1,
  input  D2,
  input  D3,
  input  D4,
  input  D5,
  input  D6,
  input  T4,
  input  T5,
  input  T6,
  input  r,
  output SC_Clear
);

  wire and_1_out, and_2_out, and_3_out, and_4_out, and_5_out, and_6_out, and_7_out;

  and and_1 (and_1_out, D0, T5);
  and and_2 (and_2_out, D1, T5);
  and and_3 (and_3_out, D2, T5);
  and and_4 (and_4_out, D3, T4);
  and and_5 (and_5_out, D4, T4);
  and and_6 (and_6_out, D5, T5);
  and and_7 (and_7_out, D6, T6);
  or or_1 (SC_Clear, r, and_1_out, and_2_out, and_3_out, and_4_out, and_5_out, and_6_out, and_7_out);
endmodule

module Register_15 (
  input  [15:0] Register,
  output _15th
);
endmodule

module _0_Register (
  input  [15:0] Register,
  output Zero_Register
);

  wire not_1_out, or_1_out;

  or or_1 (or_1_out, Register[15], Register[14], Register[13], Register[12], Register[11], Register[10], Register[9], Register[8], Register[7], Register[6], Register[5], Register[4], Register[3], Register[2], Register[1], Register[0]);
  not not_1 (not_1_out, or_1_out);
endmodule

module AC_Control (
  input  T5,
  input  D0,
  input  D1,
  input  D2,
  input  r,
  input  B11,
  input  B9,
  input  B7,
  input  B6,
  input  B5,
  output LDA,
  output CLR,
  output INR,
  output [7:0] ALU
);

  and and_1 (ALU[0], D0, T5);
  and and_2 (ALU[1], D1, T5);
  and and_3 (ALU[2], D2, T5);
  and and_4 (ALU[3], r, B9);
  and and_5 (ALU[4], r, B7);
  and and_6 (ALU[5], r, B6);
  and and_7 (ALU[6], r, B11);
  and and_8 (ALU[7], r, B5);
  or or_1 (LDA, ALU[0], ALU[1], ALU[2], ALU[3], ALU[4], ALU[5]);

  assign CLR = ALU[6];
  assign INR = ALU[7];
endmodule

// ALU
module ALU16bit (
  input  [5:0] CU_inputs,
  input  E_in,
  input  [15:0] DR,
  input  [15:0] AC_i_1,
  input  [15:0] AC_i_1_2,
  input  [15:0] AC,
  output [15:0] AC_i,
  output E_out
);

  wire alu1bit_1_c_i_1, alu1bit_2_c_i_1, alu1bit_3_c_i_1, alu1bit_4_c_i_1, alu1bit_5_c_i_1, alu1bit_6_c_i_1,
       alu1bit_7_c_i_1, alu1bit_8_c_i_1, alu1bit_9_c_i_1, alu1bit_10_c_i_1, alu1bit_11_c_i_1,
       alu1bit_12_c_i_1, alu1bit_13_c_i_1, alu1bit_14_c_i_1, alu1bit_15_c_i_1;

  ALU1bit alu1bit_1 (
    .AC_i(AC[0]), .AND(CU_inputs[0]), .ADD(CU_inputs[1]), .DR_E(CU_inputs[2]), .Complement(CU_inputs[3]),
    .SHift_r(CU_inputs[4]), .AC_i_1(AC_i_1[0]), .Shift_l(CU_inputs[5]), .AC_i_1_2(AC_i_1_2[0]),
    .AC__i(AC_i[0]), .DR_i(DR[0]), .C_i(E_in), .C_i_1(alu1bit_1_c_i_1));
  ALU1bit alu1bit_2 (
    .AC_i(AC[1]), .AND(CU_inputs[0]), .ADD(CU_inputs[1]), .DR_E(CU_inputs[2]), .Complement(CU_inputs[3]),
    .SHift_r(CU_inputs[4]), .AC_i_1(AC_i_1[1]), .Shift_l(CU_inputs[5]), .AC_i_1_2(AC_i_1_2[1]),
    .AC__i(AC_i[1]), .DR_i(DR[15]), .C_i(alu1bit_1_c_i_1), .C_i_1(alu1bit_2_c_i_1));
  ALU1bit alu1bit_3 (
    .AC_i(AC[2]), .AND(CU_inputs[0]), .ADD(CU_inputs[1]), .DR_E(CU_inputs[2]), .Complement(CU_inputs[3]),
    .SHift_r(CU_inputs[4]), .AC_i_1(AC_i_1[2]), .Shift_l(CU_inputs[5]), .AC_i_1_2(AC_i_1_2[2]),
    .AC__i(AC_i[2]), .DR_i(DR[14]), .C_i(alu1bit_2_c_i_1), .C_i_1(alu1bit_3_c_i_1));
  ALU1bit alu1bit_4 (
    .AC_i(AC[3]), .AND(CU_inputs[0]), .ADD(CU_inputs[1]), .DR_E(CU_inputs[2]), .Complement(CU_inputs[3]),
    .SHift_r(CU_inputs[4]), .AC_i_1(AC_i_1[3]), .Shift_l(CU_inputs[5]), .AC_i_1_2(AC_i_1_2[3]),
    .AC__i(AC_i[3]), .DR_i(DR[13]), .C_i(alu1bit_3_c_i_1), .C_i_1(alu1bit_4_c_i_1));
  ALU1bit alu1bit_5 (
    .AC_i(AC[4]), .AND(CU_inputs[0]), .ADD(CU_inputs[1]), .DR_E(CU_inputs[2]), .Complement(CU_inputs[3]),
    .SHift_r(CU_inputs[4]), .AC_i_1(AC_i_1[4]), .Shift_l(CU_inputs[5]), .AC_i_1_2(AC_i_1_2[4]),
    .AC__i(AC_i[4]), .DR_i(DR[12]), .C_i(alu1bit_4_c_i_1), .C_i_1(alu1bit_5_c_i_1));
  ALU1bit alu1bit_6 (
    .AC_i(AC[5]), .AND(CU_inputs[0]), .ADD(CU_inputs[1]), .DR_E(CU_inputs[2]), .Complement(CU_inputs[3]),
    .SHift_r(CU_inputs[4]), .AC_i_1(AC_i_1[5]), .Shift_l(CU_inputs[5]), .AC_i_1_2(AC_i_1_2[5]),
    .AC__i(AC_i[5]), .DR_i(DR[11]), .C_i(alu1bit_5_c_i_1), .C_i_1(alu1bit_6_c_i_1));
  ALU1bit alu1bit_7 (
    .AC_i(AC[6]), .AND(CU_inputs[0]), .ADD(CU_inputs[1]), .DR_E(CU_inputs[2]), .Complement(CU_inputs[3]),
    .SHift_r(CU_inputs[4]), .AC_i_1(AC_i_1[6]), .Shift_l(CU_inputs[5]), .AC_i_1_2(AC_i_1_2[6]),
    .AC__i(AC_i[6]), .DR_i(DR[10]), .C_i(alu1bit_6_c_i_1), .C_i_1(alu1bit_7_c_i_1));
  ALU1bit alu1bit_8 (
    .AC_i(AC[7]), .AND(CU_inputs[0]), .ADD(CU_inputs[1]), .DR_E(CU_inputs[2]), .Complement(CU_inputs[3]),
    .SHift_r(CU_inputs[4]), .AC_i_1(AC_i_1[7]), .Shift_l(CU_inputs[5]), .AC_i_1_2(AC_i_1_2[7]),
    .AC__i(AC_i[7]), .DR_i(DR[9]), .C_i(alu1bit_7_c_i_1), .C_i_1(alu1bit_8_c_i_1));
  ALU1bit alu1bit_9 (
    .AC_i(AC[8]), .AND(CU_inputs[0]), .ADD(CU_inputs[1]), .DR_E(CU_inputs[2]), .Complement(CU_inputs[3]),
    .SHift_r(CU_inputs[4]), .AC_i_1(AC_i_1[8]), .Shift_l(CU_inputs[5]), .AC_i_1_2(AC_i_1_2[8]),
    .AC__i(AC_i[8]), .DR_i(DR[8]), .C_i(alu1bit_8_c_i_1), .C_i_1(alu1bit_9_c_i_1));
  ALU1bit alu1bit_10 (
    .AC_i(AC[9]), .AND(CU_inputs[0]), .ADD(CU_inputs[1]), .DR_E(CU_inputs[2]), .Complement(CU_inputs[3]),
    .SHift_r(CU_inputs[4]), .AC_i_1(AC_i_1[9]), .Shift_l(CU_inputs[5]), .AC_i_1_2(AC_i_1_2[9]),
    .AC__i(AC_i[9]), .DR_i(DR[7]), .C_i(alu1bit_9_c_i_1), .C_i_1(alu1bit_10_c_i_1));
  ALU1bit alu1bit_11 (
    .AC_i(AC[10]), .AND(CU_inputs[0]), .ADD(CU_inputs[1]), .DR_E(CU_inputs[2]), .Complement(CU_inputs[3]),
    .SHift_r(CU_inputs[4]), .AC_i_1(AC_i_1[10]), .Shift_l(CU_inputs[5]), .AC_i_1_2(AC_i_1_2[10]),
    .AC__i(AC_i[10]), .DR_i(DR[6]), .C_i(alu1bit_10_c_i_1), .C_i_1(alu1bit_11_c_i_1));
  ALU1bit alu1bit_12 (
    .AC_i(AC[11]), .AND(CU_inputs[0]), .ADD(CU_inputs[1]), .DR_E(CU_inputs[2]), .Complement(CU_inputs[3]),
    .SHift_r(CU_inputs[4]), .AC_i_1(AC_i_1[11]), .Shift_l(CU_inputs[5]), .AC_i_1_2(AC_i_1_2[11]),
    .AC__i(AC_i[11]), .DR_i(DR[5]), .C_i(alu1bit_11_c_i_1), .C_i_1(alu1bit_12_c_i_1));
  ALU1bit alu1bit_13 (
    .AC_i(AC[12]), .AND(CU_inputs[0]), .ADD(CU_inputs[1]), .DR_E(CU_inputs[2]), .Complement(CU_inputs[3]),
    .SHift_r(CU_inputs[4]), .AC_i_1(AC_i_1[12]), .Shift_l(CU_inputs[5]), .AC_i_1_2(AC_i_1_2[12]),
    .AC__i(AC_i[12]), .DR_i(DR[4]), .C_i(alu1bit_12_c_i_1), .C_i_1(alu1bit_13_c_i_1));
  ALU1bit alu1bit_14 (
    .AC_i(AC[13]), .AND(CU_inputs[0]), .ADD(CU_inputs[1]), .DR_E(CU_inputs[2]), .Complement(CU_inputs[3]),
    .SHift_r(CU_inputs[4]), .AC_i_1(AC_i_1[13]), .Shift_l(CU_inputs[5]), .AC_i_1_2(AC_i_1_2[13]),
    .AC__i(AC_i[13]), .DR_i(DR[3]), .C_i(alu1bit_13_c_i_1), .C_i_1(alu1bit_14_c_i_1));
  ALU1bit alu1bit_15 (
    .AC_i(AC[14]), .AND(CU_inputs[0]), .ADD(CU_inputs[1]), .DR_E(CU_inputs[2]), .Complement(CU_inputs[3]),
    .SHift_r(CU_inputs[4]), .AC_i_1(AC_i_1[14]), .Shift_l(CU_inputs[5]), .AC_i_1_2(AC_i_1_2[14]),
    .AC__i(AC_i[14]), .DR_i(DR[2]), .C_i(alu1bit_14_c_i_1), .C_i_1(alu1bit_15_c_i_1));
  ALU1bit alu1bit_16 (
    .AC_i(AC[15]), .AND(CU_inputs[0]), .ADD(CU_inputs[1]), .DR_E(CU_inputs[2]), .Complement(CU_inputs[3]),
    .SHift_r(CU_inputs[4]), .AC_i_1(AC_i_1[15]), .Shift_l(CU_inputs[5]), .AC_i_1_2(AC_i_1_2[15]),
    .AC__i(AC_i[15]), .DR_i(DR[1]), .C_i(alu1bit_15_c_i_1), .C_i_1(E_out));
endmodule

module ALU1bit (
  input  DR_i,
  input  C_i,
  input  AC_i,
  input  AND,
  input  ADD,
  input  DR_E,
  input  Complement,
  input  SHift_r,
  input  AC_i_1,
  input  Shift_l,
  input  AC_i_1_2,
  output AC__i,
  output C_i_1
);

  wire ADD_out, adder_1_out, AND_out, COM_out, DR_out, not_1_out, SHL_out, SHR_out;

  Adder #(.width(1)) adder_1 (.a(AC_i), .b(DR_i), .out(adder_1_out), .cin(C_i), .cout(C_i_1));
  not not_1 (not_1_out, AC_i);
  and u_AND (AND_out, AC_i, AND, DR_i);
  and u_ADD (ADD_out, ADD, adder_1_out);
  and DR (DR_out, DR_E, DR_i);
  and COM (COM_out, Complement, not_1_out);
  and SHR (SHR_out, SHift_r, AC_i_1);
  and SHL (SHL_out, Shift_l, AC_i_1_2);
  or or_1 (AC__i, AND_out, ADD_out, DR_out, COM_out, SHR_out, SHL_out);
endmodule
