// Logisim project Project-Alu.circ as structural Verilog
module ALU (
  input  DR_i,
  input  C_i,
  input  AC_i,
  input  AND,
  input  ADD,
  input  DR_E,
  input  Complement,
  input  C_i_1,
  input  SHift_r,
  input  AC_i_1,
  input  Shift_l,
  input  AC_i_1_2,
  output AC__i
);

  wire ADD_out, adder_1_out, AND_out, COM_out, DR_out, not_1_out, SHL_out, SHR_out;

  Adder #(.width(1)) adder_1 (.a(AC_i), .b(DR_i), .out(adder_1_out), .cin(C_i), .cout(C_i_1));
  not not_1 (not_1_out, AC_i);
  and u_AND (AND_out, AC_i, AND, DR_i);
  and u_ADD (ADD_out, ADD, adder_1_out);
  and DR (DR_out, DR_E, DR_i);
  and COM (COM_out, Complement, not_1_out);
  and SHR (SHR_out, SHift_r, AC_i_1);
  and SHL (SHL_out, Shift_l, AC_i_1_2);
  or or_1 (AC__i, AND_out, ADD_out, DR_out, COM_out, SHR_out, SHL_out);
endmodule

module _16BitAlu (
  input  [5:0] CU_inputs,
  input  E_in,
  input  [15:0] DR,
  input  AC_i,
  input  [15:0] AC_i_1,
  input  [15:0] AC_i_1_2,
  input  E_out,
  output [15:0] AC_i_2
);

  wire undriven, undriven_2, undriven_3, undriven_4, undriven_5, undriven_6, undriven_7, undriven_8,
       undriven_9, undriven_10, undriven_11, undriven_12, undriven_13;

  ALU alu_1 (
    .AND(CU_inputs[0]), .ADD(CU_inputs[1]), .DR_E(CU_inputs[2]), .Complement(CU_inputs[3]),
    .SHift_r(CU_inputs[4]), .AC_i_1(AC_i_1[0]), .Shift_l(CU_inputs[5]), .AC_i_1_2(AC_i_1_2[0]), .DR_i(DR[0]),
    .C_i(E_in), .C_i_1(undriven), .AC__i(AC_i_2[0]), .AC_i(AC_i));
  ALU alu_2 (
    .AND(CU_inputs[0]), .ADD(CU_inputs[1]), .DR_E(CU_inputs[2]), .Complement(CU_inputs[3]),
    .SHift_r(CU_inputs[4]), .AC_i_1(AC_i_1[1]), .Shift_l(CU_inputs[5]), .AC_i_1_2(AC_i_1_2[1]),
    .DR_i(DR[15]), .C_i(undriven), .C_i_1(undriven_2), .AC__i(AC_i_2[1]));  // open: AC_i
  ALU alu_3 (
    .AND(CU_inputs[0]), .ADD(CU_inputs[1]), .DR_E(CU_inputs[2]), .Complement(CU_inputs[3]),
    .SHift_r(CU_inputs[4]), .AC_i_1(AC_i_1[2]), .Shift_l(CU_inputs[5]), .AC_i_1_2(AC_i_1_2[2]),
    .DR_i(DR[14]), .C_i(undriven_2), .C_i_1(undriven_3), .AC__i(AC_i_2[2]));  // open: AC_i
  ALU alu_4 (
    .AND(CU_inputs[0]), .ADD(CU_inputs[1]), .DR_E(CU_inputs[2]), .Complement(CU_inputs[3]),
    .SHift_r(CU_inputs[4]), .AC_i_1(AC_i_1[3]), .Shift_l(CU_inputs[5]), .AC_i_1_2(AC_i_1_2[3]),
    .DR_i(DR[13]), .C_i(undriven_3), .C_i_1(undriven_4), .AC__i(AC_i_2[3]));  // open: AC_i
  ALU alu_5 (
    .AND(CU_inputs[0]), .ADD(CU_inputs[1]), .DR_E(CU_inputs[2]), .Complement(CU_inputs[3]),
    .SHift_r(CU_inputs[4]), .AC_i_1(AC_i_1[4]), .Shift_l(CU_inputs[5]), .AC_i_1_2(AC_i_1_2[4]),
    .DR_i(DR[12]), .C_i(undriven_4), .C_i_1(undriven_5), .AC__i(AC_i_2[4]));  // open: AC_i
  ALU alu_6 (
    .AND(CU_inputs[0]), .ADD(CU_inputs[1]), .DR_E(CU_inputs[2]), .Complement(CU_inputs[3]),
    .SHift_r(CU_inputs[4]), .AC_i_1(AC_i_1[5]), .Shift_l(CU_inputs[5]), .AC_i_1_2(AC_i_1_2[5]),
    .DR_i(DR[11]), .C_i(undriven_5), .C_i_1(undriven_6), .AC__i(AC_i_2[5]));  // open: AC_i
  ALU alu_7 (
    .AND(CU_inputs[0]), .ADD(CU_inputs[1]), .DR_E(CU_inputs[2]), .Complement(CU_inputs[3]),
    .SHift_r(CU_inputs[4]), .AC_i_1(AC_i_1[6]), .Shift_l(CU_inputs[5]), .AC_i_1_2(AC_i_1_2[6]),
    .DR_i(DR[10]), .C_i(undriven_6), .C_i_1(undriven_7), .AC__i(AC_i_2[6]));  // open: AC_i
  ALU alu_8 (
    .AND(CU_inputs[0]), .ADD(CU_inputs[1]), .DR_E(CU_inputs[2]), .Complement(CU_inputs[3]),
    .SHift_r(CU_inputs[4]), .AC_i_1(AC_i_1[7]), .Shift_l(CU_inputs[5]), .AC_i_1_2(AC_i_1_2[7]), .DR_i(DR[9]),
    .C_i(undriven_7), .C_i_1(undriven_8), .AC__i(AC_i_2[7]));  // open: AC_i
  ALU alu_9 (
    .AND(CU_inputs[0]), .ADD(CU_inputs[1]), .DR_E(CU_inputs[2]), .Complement(CU_inputs[3]),
    .SHift_r(CU_inputs[4]), .AC_i_1(AC_i_1[8]), .Shift_l(CU_inputs[5]), .AC_i_1_2(AC_i_1_2[8]), .DR_i(DR[8]),
    .C_i(undriven_8), .C_i_1(undriven_9), .AC__i(AC_i_2[8]));  // open: AC_i
  ALU alu_10 (
    .AND(CU_inputs[0]), .ADD(CU_inputs[1]), .DR_E(CU_inputs[2]), .Complement(CU_inputs[3]),
    .SHift_r(CU_inputs[4]), .AC_i_1(AC_i_1[9]), .Shift_l(CU_inputs[5]), .AC_i_1_2(AC_i_1_2[9]), .DR_i(DR[7]),
    .C_i(undriven_9), .C_i_1(undriven_10), .AC__i(AC_i_2[9]));  // open: AC_i
  ALU alu_11 (
    .AND(CU_inputs[0]), .ADD(CU_inputs[1]), .DR_E(CU_inputs[2]), .Complement(CU_inputs[3]),
    .SHift_r(CU_inputs[4]), .AC_i_1(AC_i_1[10]), .Shift_l(CU_inputs[5]), .AC_i_1_2(AC_i_1_2[10]),
    .DR_i(DR[6]), .C_i(undriven_10), .C_i_1(undriven_11), .AC__i(AC_i_2[10]));  // open: AC_i
  ALU alu_12 (
    .AND(CU_inputs[0]), .ADD(CU_inputs[1]), .DR_E(CU_inputs[2]), .Complement(CU_inputs[3]),
    .SHift_r(CU_inputs[4]), .AC_i_1(AC_i_1[11]), .Shift_l(CU_inputs[5]), .AC_i_1_2(AC_i_1_2[11]),
    .DR_i(DR[5]), .C_i(undriven_11), .C_i_1(undriven_12), .AC__i(AC_i_2[11]));  // open: AC_i
  ALU alu_13 (
    .AND(CU_inputs[0]), .ADD(CU_inputs[1]), .DR_E(CU_inputs[2]), .Complement(CU_inputs[3]),
    .SHift_r(CU_inputs[4]), .AC_i_1(AC_i_1[12]), .Shift_l(CU_inputs[5]), .AC_i_1_2(AC_i_1_2[12]),
    .DR_i(DR[4]), .C_i(undriven_12), .C_i_1(undriven_13), .AC__i(AC_i_2[12]));  // open: AC_i
  ALU alu_14 (
    .AND(CU_inputs[0]), .ADD(CU_inputs[1]), .DR_E(CU_inputs[2]), .Complement(CU_inputs[3]),
    .SHift_r(CU_inputs[4]), .AC_i_1(AC_i_1[13]), .Shift_l(CU_inputs[5]), .AC_i_1_2(AC_i_1_2[13]),
    .DR_i(DR[3]), .C_i(undriven_13), .AC__i(AC_i_2[13]));  // open: C_i_1, AC_i
  ALU alu_15 (
    .AND(CU_inputs[0]), .ADD(CU_inputs[1]), .DR_E(CU_inputs[2]), .Complement(CU_inputs[3]),
    .SHift_r(CU_inputs[4]), .AC_i_1(AC_i_1[14]), .Shift_l(CU_inputs[5]), .AC_i_1_2(AC_i_1_2[14]),
    .DR_i(DR[2]), .AC__i(AC_i_2[14]));  // open: C_i, C_i_1, AC_i
  ALU alu_16 (
    .AND(CU_inputs[0]), .ADD(CU_inputs[1]), .DR_E(CU_inputs[2]), .Complement(CU_inputs[3]),
    .SHift_r(CU_inputs[4]), .AC_i_1(AC_i_1[15]), .Shift_l(CU_inputs[5]), .AC_i_1_2(AC_i_1_2[15]),
    .DR_i(DR[1]), .C_i_1(E_out), .AC__i(AC_i_2[15]));  // open: C_i, AC_i
endmodule
