// Logisim project Project-Alu.circ as structural Verilog
module ALU (
  input  DR_i,
  input  C_i,
  input  LD,
  input  AND,
  input  ADD,
  input  DR_E,
  input  Complement,
  input  C_i_1,
  input  SHift_r,
  input  AC_i_1,
  input  CP,
  input  Shift_l,
  input  AC_i_1_2,
  output AC__i,
  output AC__i_2
);

  wire ADD_out, adder_1_out, and_2_out, and_3_out, AND_out, COM_out, DR_out, not_1_out, not_2_out, or_1_out,
       SHL_out, SHR_out;

  Adder #(.width(1)) adder_1 (.a(AC__i), .b(DR_i), .out(adder_1_out), .cin(C_i), .cout(C_i_1));
  not not_1 (not_1_out, AC__i);
  and u_AND (AND_out, AC__i, AND, DR_i);
  and u_ADD (ADD_out, ADD, adder_1_out);
  and DR (DR_out, DR_E, DR_i);
  and COM (COM_out, Complement, not_1_out);
  and SHR (SHR_out, SHift_r, AC_i_1);
  and SHL (SHL_out, Shift_l, AC_i_1_2);
  or or_1 (or_1_out, AND_out, ADD_out, DR_out, COM_out, SHR_out, SHL_out);
  not not_2 (not_2_out, or_1_out);
  and and_2 (and_2_out, LD, or_1_out);
  and and_3 (and_3_out, not_2_out, LD);
  J_K_Flip_Flop AC_i (.J(and_2_out), .clk(CP), .K(and_3_out), .Q(AC__i));  // open: Qn, preset, en, reset

  assign AC__i_2 = AC__i;
endmodule

module _16BitAlu (
  input  [5:0] CU_inputs,
  input  E_in,
  input  [15:0] DR,
  input  cp,
  input  E_out,
  output E_AC_i_1,
  output E_AC_i_1_2
);

  wire alu_1_ac__i, alu_2_ac__i, alu_2_ac__i_2, alu_3_ac__i, alu_3_ac__i_2, alu_4_ac__i, alu_4_ac__i_2,
       alu_5_ac__i, alu_5_ac__i_2, alu_6_ac__i, alu_6_ac__i_2, alu_7_ac__i, alu_7_ac__i_2, alu_8_ac__i,
       alu_8_ac__i_2, alu_9_ac__i, alu_9_ac__i_2, alu_10_ac__i, alu_10_ac__i_2, alu_11_ac__i, alu_11_ac__i_2,
       alu_12_ac__i, alu_12_ac__i_2, alu_13_ac__i, alu_13_ac__i_2, alu_14_ac__i, alu_14_ac__i_2,
       alu_15_ac__i, alu_15_ac__i_2, alu_16_ac__i_2, undriven, undriven_2, undriven_3, undriven_4,
       undriven_5, undriven_6, undriven_7, undriven_8, undriven_9, undriven_10, undriven_11, undriven_12,
       undriven_13, undriven_14, undriven_15, undriven_16;

  ALU alu_1 (
    .AND(CU_inputs[0]), .ADD(CU_inputs[1]), .DR_E(CU_inputs[2]), .Complement(CU_inputs[3]),
    .SHift_r(CU_inputs[4]), .AC_i_1(alu_2_ac__i_2), .Shift_l(CU_inputs[5]), .AC_i_1_2(E_AC_i_1),
    .DR_i(DR[0]), .C_i(E_in), .LD(undriven), .C_i_1(undriven_2), .CP(cp), .AC__i(alu_1_ac__i));  // open: AC__i_2
  ALU alu_2 (
    .AND(CU_inputs[0]), .ADD(CU_inputs[1]), .DR_E(CU_inputs[2]), .Complement(CU_inputs[3]),
    .SHift_r(CU_inputs[4]), .AC_i_1(alu_3_ac__i_2), .Shift_l(CU_inputs[5]), .AC_i_1_2(alu_1_ac__i),
    .DR_i(DR[15]), .C_i(undriven_2), .LD(undriven), .C_i_1(undriven_3), .CP(cp), .AC__i(alu_2_ac__i),
    .AC__i_2(alu_2_ac__i_2));
  ALU alu_3 (
    .AND(CU_inputs[0]), .ADD(CU_inputs[1]), .DR_E(CU_inputs[2]), .Complement(CU_inputs[3]),
    .SHift_r(CU_inputs[4]), .AC_i_1(alu_4_ac__i_2), .Shift_l(CU_inputs[5]), .AC_i_1_2(alu_2_ac__i),
    .DR_i(DR[14]), .C_i(undriven_3), .LD(undriven), .C_i_1(undriven_4), .CP(cp), .AC__i(alu_3_ac__i),
    .AC__i_2(alu_3_ac__i_2));
  ALU alu_4 (
    .AND(CU_inputs[0]), .ADD(CU_inputs[1]), .DR_E(CU_inputs[2]), .Complement(CU_inputs[3]),
    .SHift_r(CU_inputs[4]), .AC_i_1(alu_5_ac__i_2), .Shift_l(CU_inputs[5]), .AC_i_1_2(alu_3_ac__i),
    .DR_i(DR[13]), .C_i(undriven_4), .LD(undriven), .C_i_1(undriven_5), .CP(cp), .AC__i(alu_4_ac__i),
    .AC__i_2(alu_4_ac__i_2));
  ALU alu_5 (
    .AND(CU_inputs[0]), .ADD(CU_inputs[1]), .DR_E(CU_inputs[2]), .Complement(CU_inputs[3]),
    .SHift_r(CU_inputs[4]), .AC_i_1(alu_6_ac__i_2), .Shift_l(CU_inputs[5]), .AC_i_1_2(alu_4_ac__i),
    .DR_i(DR[12]), .C_i(undriven_5), .LD(undriven), .C_i_1(undriven_6), .CP(cp), .AC__i(alu_5_ac__i),
    .AC__i_2(alu_5_ac__i_2));
  ALU alu_6 (
    .AND(CU_inputs[0]), .ADD(CU_inputs[1]), .DR_E(CU_inputs[2]), .Complement(CU_inputs[3]),
    .SHift_r(CU_inputs[4]), .AC_i_1(alu_7_ac__i_2), .Shift_l(CU_inputs[5]), .AC_i_1_2(alu_5_ac__i),
    .DR_i(DR[11]), .C_i(undriven_6), .LD(undriven), .C_i_1(undriven_7), .CP(cp), .AC__i(alu_6_ac__i),
    .AC__i_2(alu_6_ac__i_2));
  ALU alu_7 (
    .AND(CU_inputs[0]), .ADD(CU_inputs[1]), .DR_E(CU_inputs[2]), .Complement(CU_inputs[3]),
    .SHift_r(CU_inputs[4]), .AC_i_1(alu_8_ac__i_2), .Shift_l(CU_inputs[5]), .AC_i_1_2(alu_6_ac__i),
    .DR_i(DR[10]), .C_i(undriven_7), .LD(undriven), .C_i_1(undriven_8), .CP(cp), .AC__i(alu_7_ac__i),
    .AC__i_2(alu_7_ac__i_2));
  ALU alu_8 (
    .AND(CU_inputs[0]), .ADD(CU_inputs[1]), .DR_E(CU_inputs[2]), .Complement(CU_inputs[3]),
    .SHift_r(CU_inputs[4]), .AC_i_1(alu_9_ac__i_2), .Shift_l(CU_inputs[5]), .AC_i_1_2(alu_7_ac__i),
    .DR_i(DR[9]), .C_i(undriven_8), .LD(undriven), .C_i_1(undriven_9), .CP(cp), .AC__i(alu_8_ac__i),
    .AC__i_2(alu_8_ac__i_2));
  ALU alu_9 (
    .AND(CU_inputs[0]), .ADD(CU_inputs[1]), .DR_E(CU_inputs[2]), .Complement(CU_inputs[3]),
    .SHift_r(CU_inputs[4]), .AC_i_1(alu_10_ac__i_2), .Shift_l(CU_inputs[5]), .AC_i_1_2(alu_8_ac__i),
    .DR_i(DR[8]), .C_i(undriven_9), .LD(undriven), .C_i_1(undriven_10), .CP(cp), .AC__i(alu_9_ac__i),
    .AC__i_2(alu_9_ac__i_2));
  ALU alu_10 (
    .AND(CU_inputs[0]), .ADD(CU_inputs[1]), .DR_E(CU_inputs[2]), .Complement(CU_inputs[3]),
    .SHift_r(CU_inputs[4]), .AC_i_1(alu_11_ac__i_2), .Shift_l(CU_inputs[5]), .AC_i_1_2(alu_9_ac__i),
    .DR_i(DR[7]), .C_i(undriven_10), .LD(undriven), .C_i_1(undriven_11), .CP(cp), .AC__i(alu_10_ac__i),
    .AC__i_2(alu_10_ac__i_2));
  ALU alu_11 (
    .AND(CU_inputs[0]), .ADD(CU_inputs[1]), .DR_E(CU_inputs[2]), .Complement(CU_inputs[3]),
    .SHift_r(CU_inputs[4]), .AC_i_1(alu_12_ac__i_2), .Shift_l(CU_inputs[5]), .AC_i_1_2(alu_10_ac__i),
    .DR_i(DR[6]), .C_i(undriven_11), .LD(undriven), .C_i_1(undriven_12), .CP(cp), .AC__i(alu_11_ac__i),
    .AC__i_2(alu_11_ac__i_2));
  ALU alu_12 (
    .AND(CU_inputs[0]), .ADD(CU_inputs[1]), .DR_E(CU_inputs[2]), .Complement(CU_inputs[3]),
    .SHift_r(CU_inputs[4]), .AC_i_1(alu_13_ac__i_2), .Shift_l(CU_inputs[5]), .AC_i_1_2(alu_11_ac__i),
    .DR_i(DR[5]), .C_i(undriven_12), .C_i_1(undriven_13), .CP(cp), .AC__i(alu_12_ac__i),
    .AC__i_2(alu_12_ac__i_2));  // open: LD
  ALU alu_13 (
    .AND(CU_inputs[0]), .ADD(CU_inputs[1]), .DR_E(CU_inputs[2]), .Complement(CU_inputs[3]),
    .SHift_r(CU_inputs[4]), .AC_i_1(alu_14_ac__i_2), .Shift_l(CU_inputs[5]), .AC_i_1_2(alu_12_ac__i),
    .DR_i(DR[4]), .C_i(undriven_13), .LD(undriven), .C_i_1(undriven_14), .CP(cp), .AC__i(alu_13_ac__i),
    .AC__i_2(alu_13_ac__i_2));
  ALU alu_14 (
    .AND(CU_inputs[0]), .ADD(CU_inputs[1]), .DR_E(CU_inputs[2]), .Complement(CU_inputs[3]),
    .SHift_r(CU_inputs[4]), .AC_i_1(alu_15_ac__i_2), .Shift_l(CU_inputs[5]), .AC_i_1_2(alu_13_ac__i),
    .DR_i(DR[3]), .C_i(undriven_14), .LD(undriven), .C_i_1(undriven_15), .CP(cp), .AC__i(alu_14_ac__i),
    .AC__i_2(alu_14_ac__i_2));
  ALU alu_15 (
    .AND(CU_inputs[0]), .ADD(CU_inputs[1]), .DR_E(CU_inputs[2]), .Complement(CU_inputs[3]),
    .SHift_r(CU_inputs[4]), .AC_i_1(alu_16_ac__i_2), .Shift_l(CU_inputs[5]), .AC_i_1_2(alu_14_ac__i),
    .DR_i(DR[2]), .C_i(undriven_15), .LD(undriven), .C_i_1(undriven_16), .CP(cp), .AC__i(alu_15_ac__i),
    .AC__i_2(alu_15_ac__i_2));
  ALU alu_16 (
    .AND(CU_inputs[0]), .ADD(CU_inputs[1]), .DR_E(CU_inputs[2]), .Complement(CU_inputs[3]),
    .SHift_r(CU_inputs[4]), .AC_i_1(E_AC_i_1_2), .Shift_l(CU_inputs[5]), .AC_i_1_2(alu_15_ac__i),
    .DR_i(DR[1]), .C_i(undriven_16), .LD(undriven), .C_i_1(E_out), .CP(cp), .AC__i_2(alu_16_ac__i_2));  // open: AC__i
endmodule
